# Fritzing sketch momentary (saved by Fritzing 0.9.9b)
breadboards: 1

parts:
  Part6 = Adafruit HUZZAH32 ESP32 Feather [part_number="Adafruit #3405"]
  S1 = Momentary Switch [package=ksa_sealed_tac_switch]
  R1 = Resistor [tolerance=±5% power=0.25 resistance=10k package=THT]

nets:
  N1: Part6.A2_I34, S1.4, R1.Pin_1
  N2: Part6.GND, R1.Pin_0
  N3: Part6.3.3V, S1.2
